# Fritzing sketch Transmisor (saved by Fritzing 0.9.4)
breadboards: 1

parts:
  Componente1 = Arduino Uno (Rev3)
  BC547A = NPN-Transistor [package="TO92 [THT]"]
  R1 = Resistor [tolerance=±5% resistance=10 package=THT]
  LED1 = smd LED [color="Red (633nm)" package="0805 [SMD]"]
  R2 = Resistor [tolerance=±5% resistance=330 package=THT]
  R3 = Rotary Potentiometer (Large) [maximum_resistance=100kΩ package=THT]
  R4 = Rotary Potentiometer (Large) [maximum_resistance=100kΩ package=THT]
  S1 = Toggle Switch [package=THT]
  S2 = Toggle Switch [package=THT]
  AC = AC Power [voltage=5 frequency=60]
  Portadora = AC Power [voltage=5 frequency=60]
  R5 = Resistor [tolerance=±5% resistance=10 package=THT]
  U1 = MCP4725 [package=SOT23-6]  # not connected
  o1 = Module display OLED I2C 128x64 SSD1306 [package=THT]  # not connected

nets:
  N1: Componente1.A1, AC.V-
  N2: Componente1.D8, S1.COM
  N3: Componente1.GND, BC547A.E, LED1.cathode, AC.V+, Portadora.V-
  N4: BC547A.B, R1.Pin_1
  N5: BC547A.C, S2.L1, R5.Pin_0
  N6: R1.Pin_0, R3.leg2
  N7: LED1.anode, R2.Pin_0
  N8: R2.Pin_1, S2.COM
  N9: R3.leg1, R3.wiper, S1.L2
  N10: R4.leg1, R4.wiper, Portadora.V+
  N11: R4.leg2, R5.Pin_1
  N12: S1.L1, S2.L2

notes:
  AC in
  Señal
  Portadora

custom parts:
  Module display OLED I2C 128x64 SSD1306: Ecran OLED I2C SSD163 de 128x64 avec connexion I2C
